# Fritzing sketch circuit (saved by Fritzing 0.9.10b)
breadboards: 1

parts:
  Mod1 = Raspberry Pi 4B
  Part1 = BME280 Breakout
  Chirp!_Soil_Moisture_Sensor1 = Chirp! Soil Moisture Sensor v2.7.3
  Chirp!_Soil_Moisture_Sensor2 = Chirp! Soil Moisture Sensor v2.7.3
  Chirp!_Soil_Moisture_Sensor3 = Chirp! Soil Moisture Sensor v2.7.3
  Part2 = Adafruit ADS1015 12Bit I2C ADC [part_number="Adafruit #1083"]
  Mod2 = KY-019 5V Relay Module [package="Breakout board"]
  WATER_PUMP1 = water pump/motor
  Mod3 = generic-ac-power-supply [package=THT]

nets:
  3V3: Mod1.3V3, Part1.3.3V, Chirp!_Soil_Moisture_Sensor1.Pin_1, Chirp!_Soil_Moisture_Sensor2.Pin_1, Chirp!_Soil_Moisture_Sensor3.Pin_1, Part2.VDD, Mod2.+
  N1: Mod1.GPIO2, Part1.SCK/SCL, Part2.SDA
  N2: Mod1.GPIO3, Part1.SDI/SDA, Part2.SCL
  GND: Mod1.GND, Part1.GND, Chirp!_Soil_Moisture_Sensor1.pin_5, Chirp!_Soil_Moisture_Sensor2.pin_5, Chirp!_Soil_Moisture_Sensor3.pin_5, Part2.GND, Mod2.-
  N3: Mod1.GPIO22, Mod2.S
  N4: Chirp!_Soil_Moisture_Sensor1.pin_3, Part2.AIN2
  N5: Chirp!_Soil_Moisture_Sensor2.pin_3, Part2.AIN1
  N6: Chirp!_Soil_Moisture_Sensor3.pin_3, Part2.AIN0
  N7: Mod2.Common, WATER_PUMP1.pin_2
  N8: Mod2.NO, Mod3.pin3#2
  N9: WATER_PUMP1.pin_1, Mod3.pin3#3

notes:
  240V 50Hz AC
  Water reservoir
  Plant 1
  Plant 2
  Plant 3

custom parts:
  Adafruit ADS1015 12Bit I2C ADC: For microcontrollers without an analog-to-digital converter or when you want a higher-precision ADC, the ADS1015 provides 12-bit precision at 3300 samples/second over I2C. The chip can be configured as 4 single-ended input channels, or two differential channels. As a nice bonus, it even includes a programmable gain amplifier, up to x16, to help boost up smaller single/differential signals to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
  KY-019 5V Relay Module: KY-019 5V Relay module, used to control AC circuits. (Special thanks to vanepp for fixing the PCB holes and other errors)
  water pump/motor: WATER PUMP BY ARDUBLOCKTR
  generic-ac-power-supply: Generic ac power supply module. Use as is, or customize the svgs to fit your particular device (as they are all different.) Provides AC input and single DC output. PCB is generic and will need modifications if you intend to do a pcb mount.
